# Fritzing sketch Spooky-Smokey (saved by Fritzing 1.0.4)

parts:
  Part2 = 24-Channel 12-bit PWM LED Driver - SPI [part_number=1429]
  A1 = DY-HV20T
  S1 = Square Pushbutton
  Part1 = Adafruit Proto Screwshield Wingshield [part_number="Adafruit #196"]
  Gate = LED - 5mm [color="White (4500K)" current=0.030A package="5 mm [THT]"]
  Hill1 = LED - 5mm [color="White (4500K)" current=0.030A package="5 mm [THT]"]
  Hill2 = LED - 5mm [color="White (4500K)" current=0.030A package="5 mm [THT]"]
  KeyLeft = smd LED [color="White (4500K)" package="0805 [SMD]"]
  KeyRight = smd LED [color="White (4500K)" package="0805 [SMD]"]
  Moon = RGB LED - (4 legs) [color="Red (633nm)" current=0.030A package="5 mm [THT]"]
  J1 = Dagu DGServo 9g header (male) [package=THT]
  J2 = Dagu DGServo 9g header (male) [package=THT]
  GhostLeft = Basic Servo
  GhostRight = Basic Servo

nets:
  N1: Part2.LAT, Part1.D6
  GND: Part2.OE, Part2.GND, A1.Pin_2, S1.leg0, Part1.GND, J1.gnd, J2.gnd, GhostLeft.gnd, GhostRight.gnd
  N2: Part2.CLK, Part1.D5
  N3: Part2.DIN, Part1.D4
  N4: Part2.+24V, Part1.VIN, Gate.anode, Hill1.anode, Hill2.anode, KeyLeft.anode, KeyRight.anode, Moon.common_anode
  N5: Part2.PWM0, Gate.cathode
  N6: Part2.PWM1, Hill1.cathode
  N7: Part2.PWM2, Hill2.cathode
  N8: Part2.PWM9, Moon.red_cathode
  N9: Part2.PWM10, Moon.blue_cathode
  N10: Part2.PWM11, Moon.green_cathode
  N11: Part2.PWM22, KeyRight.cathode
  N12: Part2.PWM23, KeyLeft.cathode
  VCC: A1.Pin_3, A1.Pin_4, Part1.+5V, J1.Vcc, J2.Vcc, GhostLeft.vcc, GhostRight.vcc
  N13: A1.Pin_5, Part1.D2
  N14: A1.Pin_6, Part1.D3
  N15: S1.leg1, Part1.A5
  N16: Part1.D7, Part1.N$114, J1.pulse, GhostLeft.pulse
  N17: Part1.D8, Part1.N$153, J2.pulse, GhostRight.pulse

custom parts:
  24-Channel 12-bit PWM LED Driver - SPI: This breakout board for the TLC5947 PWM driver chip can control 24 separate channels of 12-bit PWM output. Designed (and ideal) for LED control, this board is NOT good for driving servos. Only three "SPI" pins are required to send data (our Arduino library shows how to to use any digital microcontroller pins). Best of all, the design is completely chainable. As long as there's enough power for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
  DY-HV20T: DY-HV20T 12V/24V Power supply10W/20W Voice Playback Module Supporting Micro SD Card MP3 Music Player for Arduino.
  Adafruit Proto Screwshield Wingshield: The next generation Proto-ScrewShield is a dual-purpose prototyping shield. Not only does it have a large 0.1" grid prototyping area but it also extends the Arduino pins to sturdy, secure, and dependable screw terminal blocks. You even get a few bonus terminals for extra GND and four 'free' terminals for whatever connections you wish! New! As of June 23, 2014 we now have an R3 update to this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
